# Fritzing sketch hbs_e (saved by Fritzing 0.9.3b)
circuit board: 6.72014cm x 5.38141cm
breadboards: 1

parts:
  Part1 = Arduino Pro Mini v13
  JP1 = Header 4 [package=jst-4-pth]
  K1 = Relay [part_number=FRS1B-S package=THT]
  Q1 = TRANSISTOR_NPN [package=to-92-ammo]
  R1 = Resistor [tolerance=±5% resistance=220 package=THT]
  SG1 = Buzzer 12mm [package=buzzer-12mm-ns]
  D1 = Rectifier Diode 10A [part_number=P1000K]
  Temp = JST-B3P-VH [part_number=JST-B3P-VH package=THT]
  Heat = JST-B3P-VH [part_number=JST-B3P-VH package=THT]
  Pump = JST-B3P-VH [part_number=JST-B3P-VH package=THT]
  12v = Screw terminal - 2 pins [package=THT]
  JP2 = Header 6 [package=molex-1x6-ra]

nets:
  5V: Part1.VCC, JP1.2, K1.COIL2, D1.cathode, Temp.pin1
  GND: Part1.GND, JP1.1, Q1.E, SG1.2, Temp.pin2, Heat.pin3, Pump.pin2, 12v.pin2, JP2.2, JP2.4, JP2.6
  N1: Part1.A4, JP1.4
  N2: Part1.A5, JP1.3
  net label: Part1.RAW, K1.C1, K1.C2, 12v.pin1
  N3: Part1.D11_PWM/MOSI, Heat.pin1
  N4: Part1.D10_PWM/SS, R1.Pin_0
  N5: Part1.D9_PWM, Temp.pin3
  N6: Part1.D8, SG1.1
  N7: Part1.D4, JP2.5
  N8: Part1.D3_PWM, JP2.3
  N9: Part1.D2, JP2.1
  N10: K1.A, Pump.pin1
  N11: K1.COIL1, Q1.C, D1.anode
  N12: Q1.B, R1.Pin_1
